# Fritzing sketch brewTime (saved by Fritzing 0.9.3b)
circuit board: 8.46667cm x 5.64444cm

parts:
  Part1 = Logic Level Converter
  Part2 = Arduino MKR1000
  Kettle = female pin header, 6 pins [form="♀ (female)"]

nets:
  N1: Part1.TX2_LV, Part2.D12_SCL
  N2: Part1.RX2_LV, Part2.D11_SDA
  GND: Part1.GND, Part2.GND, Kettle.pin4
  N3: Part1.LV, Part2.VCC
  N4: Part1.RX_LV, Part2.D8_MOSI
  N5: Part1.TX_LV, Part2.D7
  N6: Part1.RX_HV, Kettle.pin6
  N7: Part1.HV, Part2.VIN, Kettle.pin5
  N8: Part1.RX2_HV, Kettle.pin3
  N9: Part1.TX2_HV, Kettle.pin2
  N10: Part2.A0_DAC0, Kettle.pin1

notes:
  Heat signal
  VDD +5V
  GND
  Temp. Button
  Power Button
  LED -
  Heat Signal

custom parts:
  Arduino MKR1000: MKR1000 is a powerful board that combines the functionality of the Zero and the Wi-Fi Shield. It is the ideal solution for makers wanting to design IoT projects with minimal previous experience in networking
